# Fritzing sketch ultimate-tricorder (saved by Fritzing 0.9.3b)
circuit board: 10cm x 12cm
breadboards: 1

parts:
  EPORT1 = shrouded pin header, 16 pins [form="♂ (shrouded male)"]
  EPORT2 = shrouded pin header, 16 pins [form="♂ (shrouded male)"]
  J1 = female pin header, 8 pins [form="♀ (female)"]
  U1 = atmega328 [package=dip]
  U2 = atmega328 [package=dip]
  U3 = atmega328 [package=dip]
  U4 = attiny85 [package=dip]
  U5 = attiny85 [package=dip]
  U6 = attiny85 [package=dip]
  U7 = attiny85 [package=dip]

nets:
  N1: EPORT1.pin1, U3.A5
  N2: EPORT1.pin2, U3.A4
  N3: EPORT1.pin3, U3.A3
  N4: EPORT1.pin4, U3.A2
  N5: EPORT1.pin5, U3.A1
  N6: EPORT1.pin6, U3.A0
  N7: EPORT1.pin7, U3.D0_(RX)
  N8: EPORT1.pin8, U3.D1_(TX)
  N9: EPORT1.pin9, U3.GND#21
  GND: EPORT1.pin10, EPORT2.pin9, EPORT2.pin10, J1.pin1, U1.GND, U2.GND, U3.GND#7, U4.Pin_4, U5.Pin_4, U6.Pin_4, U7.Pin_4
  N10: EPORT1.pin11, U3.AVCC
  N11: EPORT1.pin12, U3.D13
  N12: EPORT1.pin13, U3.D12
  N13: EPORT1.pin14, U3.D11_(PWM)
  N14: EPORT1.pin15, U3.D10_(PWM)
  N15: EPORT1.pin16, U3.D9_(PWM)
  N16: EPORT2.pin1, U2.A5
  N17: EPORT2.pin2, U2.A4
  N18: EPORT2.pin3, U2.A3
  N19: EPORT2.pin4, U2.A2
  N20: EPORT2.pin5, U2.A1
  N21: EPORT2.pin6, U2.A0
  N22: EPORT2.pin7, U2.D0_(RX)
  N23: EPORT2.pin8, U2.D1_(TX)
  N24: EPORT2.pin11, U2.AVCC
  N25: EPORT2.pin12, U2.D13
  N26: EPORT2.pin13, U2.D12
  N27: EPORT2.pin14, U2.D11_(PWM)
  N28: EPORT2.pin15, U2.D10_(PWM)
  N29: EPORT2.pin16, U2.D9_(PWM)
  VCC: J1.pin8, U1.VCC, U2.VCC, U3.VCC, U4.Pin_8, U5.Pin_8, U6.Pin_8, U7.Pin_8
  N30: U1.D5_(PWM), U2.D6_(PWM)
  N31: U1.D6_(PWM), U2.D5_(PWM)
  N32: U1.D10_(PWM), U3.D6_(PWM)
  N33: U1.D11_(PWM), U3.D5_(PWM)
  N34: U1.A4, U3.RESET
  N35: U1.A5, U2.RESET
