# Fritzing sketch Untitled Sketch (saved by Fritzing 0.9.3b)
circuit board: 10cm x 12cm
breadboards: 1

parts:
  S1 = Pushbutton [package="[THT]"]
  S2 = Pushbutton [package="[THT]"]
  S3 = Pushbutton [package="[THT]"]
  S4 = Pushbutton [package="[THT]"]
  S5 = Pushbutton [package="[THT]"]
  S6 = Pushbutton [package="[THT]"]
  S7 = Pushbutton [package="[THT]"]
  S8 = Pushbutton [package="[THT]"]
  S9 = Pushbutton [package="[THT]"]
  S10 = Pushbutton [package="[THT]"]
  S11 = Pushbutton [package="[THT]"]
  S12 = Pushbutton [package="[THT]"]
  S13 = Pushbutton [package="[THT]"]
  S14 = Pushbutton [package="[THT]"]
  S15 = Pushbutton [package="[THT]"]
  S16 = Pushbutton [package="[THT]"]
  S17 = Pushbutton [package="[THT]"]
  S18 = Pushbutton [package="[THT]"]
  S19 = Pushbutton [package="[THT]"]
  S20 = Pushbutton [package="[THT]"]
  S21 = Pushbutton [package="[THT]"]
  S22 = Pushbutton [package="[THT]"]
  S23 = Pushbutton [package="[THT]"]
  S24 = Pushbutton [package="[THT]"]
  S25 = Pushbutton [package="[THT]"]
  S26 = Pushbutton [package="[THT]"]
  S27 = Pushbutton [package="[THT]"]
  S28 = Pushbutton [package="[THT]"]
  S29 = Pushbutton [package="[THT]"]
  S30 = Pushbutton [package="[THT]"]
  J1 = female pin header, 2 pins [form="♀ (female)"]
  U1 = 74HC595 [package="DIP16 [THT]"]
  U2 = 74HC595 [package="DIP16 [THT]"]
  U3 = 74HC595 [package="DIP16 [THT]"]
  U4 = 74HC595 [package="DIP16 [THT]"]

nets:
  N1: S1.Pin_1, S1.Pin_2, U3.Q1
  GND: S1.Pin_3, S1.Pin_4, S2.Pin_3, S2.Pin_4, S3.Pin_3, S3.Pin_4, S4.Pin_3, S4.Pin_4, S5.Pin_3, S5.Pin_4, S6.Pin_3, S6.Pin_4, S7.Pin_3, S7.Pin_4, S8.Pin_3, S8.Pin_4, S9.Pin_3, S9.Pin_4, S10.Pin_3, S10.Pin_4, S11.Pin_3, S11.Pin_4, S12.Pin_3, S12.Pin_4, S13.Pin_3, S13.Pin_4, S14.Pin_3, S14.Pin_4, S15.Pin_3, S15.Pin_4, S16.Pin_3, S16.Pin_4, S17.Pin_3, S17.Pin_4, S18.Pin_3, S18.Pin_4, S19.Pin_3, S19.Pin_4, S20.Pin_3, S20.Pin_4, S21.Pin_3, S21.Pin_4, S22.Pin_3, S22.Pin_4, S23.Pin_3, S23.Pin_4, S24.Pin_3, S24.Pin_4, S25.Pin_3, S25.Pin_4, S26.Pin_3, S26.Pin_4, S27.Pin_3, S27.Pin_4, S28.Pin_3, S28.Pin_4, S29.Pin_3, S29.Pin_4, S30.Pin_3, S30.Pin_4, J1.pin2, U1.GND, U2.GND, U3.GND, U4.GND
  N2: S2.Pin_1, S2.Pin_2, U3.Q2
  N3: S3.Pin_1, S3.Pin_2, U3.Q3
  N4: S4.Pin_1, S4.Pin_2, U3.Q4
  N5: S5.Pin_1, S5.Pin_2, U3.Q5
  N6: S6.Pin_1, S6.Pin_2, U3.Q6
  N7: S7.Pin_1, S7.Pin_2, U3.Q7
  N8: S8.Pin_1, U1.Q7
  N9: S9.Pin_1, U1.Q0
  N10: S10.Pin_1, S10.Pin_2, U2.Q0
  N11: S11.Pin_1, S11.Pin_2, U4.Q1
  N12: S12.Pin_1, S12.Pin_2, U4.Q2
  N13: S13.Pin_1, S13.Pin_2, U4.Q3
  N14: S14.Pin_1, S14.Pin_2, U4.Q4
  N15: S15.Pin_1, S15.Pin_2, U4.Q5
  N16: S16.Pin_1, S16.Pin_2, U4.Q6
  N17: S17.Pin_1, S17.Pin_2, U4.Q7
  N18: S18.Pin_1, U1.Q1
  N19: S19.Pin_1, U1.Q2
  N20: S20.Pin_1, U1.Q3
  N21: S21.Pin_1, S21.Pin_2, U2.Q1
  N22: S22.Pin_1, S22.Pin_2, U2.Q2
  N23: S23.Pin_1, S23.Pin_2, U2.Q3
  N24: S24.Pin_1, S24.Pin_2, U2.Q4
  N25: S25.Pin_1, S25.Pin_2, U2.Q5
  N26: S26.Pin_1, S26.Pin_2, U2.Q6
  N27: S27.Pin_1, S27.Pin_2, U2.Q7
  N28: S28.Pin_1, U1.Q4
  N29: S29.Pin_1, U1.Q5
  N30: S30.Pin_1, U1.Q6
  VCC: J1.pin1, U1.VCC, U2.VCC, U3.VCC, U4.VCC
